// Digital circuit CacheSetAssoc2Way2WPB.dig as structural Verilog
module CacheSetAssoc2Way2WPB (
  input  [31:0] in_1,
  output Hit,
  output [31:0] data
);

  wire hit0, hit1, mvalid0, mvalid1, priorityencoder_1_num;
  wire [8:0] cache_controller_1_p6;
  wire [19:0] mtag0, mtag1;
  wire [31:0] data0, data1, mword00, mword01, mword10, mword11;

  // Cache_Controller cache_controller_1: pin names not known; wires that end beside it: in_1, mword00, mtag0, mvalid0, mword01, cache_controller_1_p6, hit0, data0
  Cache_Controller cache_controller_2 (
    .address(in_1), .mword0(mword10), .mtag(mtag1), .mvalid(mvalid1), .mword1(mword11), .hit(hit1),
    .data(data1));  // open: index
  CacheSaMwMemory #(.applicationType("IVERILOG")) u_CacheSaMwMemory (
    .addr(cache_controller_1_p6), .w0valid(mvalid0), .w0tag(mtag0), .w0word0(mword00), .w0word1(mword01),
    .w1valid(mvalid1), .w1tag(mtag1), .w1word0(mword10), .w1word1(mword11));
  PriorityEncoder priorityencoder_1 (.in0(hit0), .in1(hit1), .num(priorityencoder_1_num));  // open: any
  and and_1 (Hit, hit0, hit1);
  Multiplexer #(.Bits(32)) multiplexer_1 (.sel(priorityencoder_1_num), .in_0(data0), .in_1(data1), .out(data));
endmodule

/* Code of CacheSaMwMemory:
module CacheSaMwMemory(
    input [8:0] addr,
    output w0valid,
    output [19:0] w0tag,
    output [31:0] w0word0,
    output [31:0] w0word1,
    output w1valid,
    output [19:0] w1tag,
    output [31:0] w1word0,
    output [31:0] w1word1
);

    reg [169:0] memory [0:511];    
    wire [169:0] data;
    
    assign data = memory[addr];
    
    assign w0valid = data[169];
    assign w1valid = data[168];
    assign w0tag = data[167:148];
    assign w1tag = data[147:128];
    
    assign w0word0 = data[127:96];
    assign w0word1 = data[95:64];
    assign w1word0 = data[63:32];
    assign w1word1 = data[31:0];
    
    initial
    begin
        memory[1] = 170'h3_00000_00001_000000e7_000000e8_000000a7_000000a8;
    end
    
endmodule
*/
