// Digital circuit Cache_Controller.dig as structural Verilog
module Cache_Controller (
  input  [31:0] address,
  input  [31:0] mword0,
  input  [19:0] mtag,
  input  mvalid,
  input  [31:0] mword1,
  output [8:0] index,
  output hit,
  output [31:0] data
);

  wire comparator_1_eq;

  Comparator #(.Bits(20)) comparator_1 (.a(address[31:12]), .b(mtag), .eq(comparator_1_eq));  // open: gt, lt
  Multiplexer #(.Bits(32)) multiplexer_1 (.sel(address[2]), .in_0(mword0), .in_1(mword1), .out(data));
  and and_1 (hit, comparator_1_eq, mvalid);
  // Pins of 8 and 9 bits meet at address[11:3]

  assign index = address[11:3];

  // Other names for the same wires on the sheet: word_offset = address[2]
endmodule
